# Fritzing sketch Untitled Sketch (saved by Fritzing 0.9.3b)
breadboards: 1

parts:
  Gizwits_WiFi_Witty_ESP-12F1 = Gizwits WiFi Witty ESP-12F
  Q1 = TRANSISTOR_PNP [package=to-92]
  R1 = Resistor [tolerance=±5% resistance=220 package="2010 [SMD]"]
  J1 = Piezo Speaker
  Componente1 = PowerBoost 500 Charger
  VCC1 = Battery block 9V  # not connected

nets:
  N1: Gizwits_WiFi_Witty_ESP-12F1.VCC, Componente1.ENABLE
  N2: Gizwits_WiFi_Witty_ESP-12F1.GND, R1.Pin_1
  N3: Q1.B, R1.Pin_0
  N4: Q1.C, J1.pin1
  N5: J1.pin2, Componente1.GND
